# Fritzing sketch weemos_hookup (saved by Fritzing 0.8.5b)
circuit board: 2.59956cm x 3.50913cm
breadboards: 1

parts:
  IR1 = TSOP312.., 314.. [package=THT]
  LED1 = LED - 5mm [color="Red (633nm)" package="5 mm [THT]"]
  LED2 = LED - 5mm [color="Red (633nm)" package="5 mm [THT]"]
  LED3 = LED - 5mm [color="Red (633nm)" package="5 mm [THT]"]
  LED4 = LED - 5mm [color="Red (633nm)" package="5 mm [THT]"]
  S1 = Pushbutton [package="[THT]"]
  R1 = Resistor [tolerance=±5% resistance=220 package=THT]
  R2 = Resistor [tolerance=±5% resistance=220 package=THT]
  Q2 = TRANSISTOR_NPN [package=to-92]
  WeMos_D1_Mini1 = WeMos D1 Mini

nets:
  N1: IR1.GND, LED1.cathode, LED4.cathode, S1.Pin_1, S1.Pin_2, WeMos_D1_Mini1.G
  N2: IR1.Vs, WeMos_D1_Mini1.3V3
  N3: IR1.Data, WeMos_D1_Mini1.D4
  N4: LED1.anode, LED3.cathode
  N5: LED2.cathode, LED4.anode
  N6: LED2.anode, R2.Pin_0
  N7: LED3.anode, R1.Pin_0
  N8: S1.Pin_3, S1.Pin_4, WeMos_D1_Mini1.D2
  N9: R1.Pin_1, R2.Pin_1, Q2.E
  N10: Q2.B, WeMos_D1_Mini1.D3
  N11: Q2.C, WeMos_D1_Mini1.5V

custom parts:
  WeMos D1 Mini: The D1 mini is a mini wifi board based on ESP-8266EX.
