# Fritzing sketch weemos_hookup_v2 (saved by Fritzing 0.8.5b)
circuit board: 2.59703cm x 3.48845cm
breadboards: 2

parts:
  IRLED1 = LTE-302 [package=lte-302]
  IRLED2 = LTE-302 [package=lte-302]
  IRLED3 = LTE-302 [package=lte-302]
  IRLED4 = LTE-302 [package=lte-302]
  R1 = Resistor [tolerance=±5% resistance=22 package=THT]
  R2 = Resistor [tolerance=±5% resistance=22 package=THT]
  CFG = Pushbutton [package="[THT]"]
  WeMos_D1_Mini1 = WeMos D1 Mini
  JP5 = Header 3 [package=molex-1x3_lock]
  JP1 = Header 2 [package=molex-1x2_lock]
  JP2 = Header 2 [package=molex-1x2_lock]
  JP3 = Header 2 [package=molex-1x2_lock]
  JP4 = Header 2 [package=molex-1x2_lock]
  IR2 = TSOP312.., 314.. [package=THT]
  C1 = Electrolytic Capacitor [capacitance=1µF package="100 mil [THT, electrolytic]"]
  NPN = TRANSISTOR_NPN [package=to-92]
  STATUS_LED_(optional) = LED - 3mm [color="Red (633nm)" package="3 mm [THT]"]
  R3 = Resistor [tolerance=±5% resistance=100 package=THT]
  JP6 = Header 2 [package=molex-1x2_lock]

nets (from the breadboard view):
  N1: IRLED1.A, IRLED2.C, JP1.2, JP2.1
  N2: IRLED1.C, IRLED3.C, CFG.Pin_1, CFG.Pin_2, WeMos_D1_Mini1.G, JP5.1, JP1.1, JP3.1, IR2.GND, C1.-
  N3: IRLED2.A, R1.Pin_0, JP2.2
  N4: IRLED3.A, IRLED4.C, JP3.2, JP4.1
  N5: IRLED4.A, R2.Pin_0, JP4.2
  N6: R1.Pin_1, R2.Pin_1, NPN.E
  N7: CFG.Pin_3, CFG.Pin_4, WeMos_D1_Mini1.D2
  N8: WeMos_D1_Mini1.3V3, JP5.2, IR2.Vs, STATUS_LED_(optional).anode, JP6.2
  N9: WeMos_D1_Mini1.5V, C1.+, NPN.C
  N10: WeMos_D1_Mini1.D3, NPN.B
  N11: WeMos_D1_Mini1.D4, JP5.3, IR2.Data
  N12: WeMos_D1_Mini1.D5, R3.Pin_1
  N13: STATUS_LED_(optional).cathode, R3.Pin_0, JP6.1

custom parts:
  WeMos D1 Mini: The D1 mini is a mini wifi board based on ESP-8266EX.
